# Fritzing sketch vectron_vr (saved by Fritzing 0.9.3b)
breadboards: 4

parts:
  U1 = IC, SIP package, 10 pins [chip_label=74ALS244AN]
  U2 = IC, SIP package, 8 pins [chip_label=74161A]
  U3 = IC, SIP package, 10 pins [chip_label=74688]
  U4 = IC, SIP package, 7 pins [chip_label=74HCT32]
  U5 = IC, SIP package, 7 pins [chip_label=7404]

nets:
  N1: U1.pin10, U2.pin8, U3.pin1, U3.pin2, U3.pin3, U3.pin4, U3.pin5, U3.pin6, U3.pin7, U3.pin8, U3.pin9, U3.pin10, U4.pin7, U5.pin7

notes:
  To 7MHz Oscillator
  To 5V DC
